# Fritzing sketch PIDFritzing (saved by Fritzing 0.9.3b)
breadboards: 1

parts:
  Part1 = Arduino Uno (Rev3)
  BAT1 = Battery Holders [package=battery-aa]
  BAT2 = Battery Holders [package=battery-aa]
  BAT3 = Battery Holders [package=battery-aa]
  BAT4 = Battery Holders [package=battery-aa]
  BAT7 = Battery Holders [package=battery-aa]
  BAT8 = Battery Holders [package=battery-aa]
  Q1 = PHOTOTRANSISTOR REFLECTIVE OBJECT SENSOR [package=qrb1114-side]
  Q2 = NPN-Transistor [package="SOT-23 [SMD]"]
  R1 = Resistor [tolerance=±5% resistance=220 package="0805 [SMD]"]
  D1 = Rectifier Diode [part_number=1N4001 package="Melf DO-213 AB [SMD]"]
  M1 = DC Motor
  U1 = POT [package=pot_mammoth]
  LCD1 = LCD screen  # not connected
  S1 = Toggle Switch [package=THT]  # not connected
  S2 = Toggle Switch [package=THT]
  LED1 = LED - 3mm [color="Red (633nm)" package="3 mm [THT]"]
  LED2 = LED - 3mm [color="Red (633nm)" package="3 mm [THT]"]
  LED3 = LED - 3mm [color="Red (633nm)" package="3 mm [THT]"]
  LED4 = LED - 3mm [color="Green (555nm)" package="3 mm [THT]"]
  LED5 = LED - 3mm [color="Red (633nm)" package="3 mm [THT]"]

nets:
  N1: Part1.A0, U1.A
  N2: Part1.D1/TX, LED3.anode
  N3: Part1.D2, LED2.anode
  N4: Part1.D3_PWM, LED5.anode
  N5: Part1.D4, LED1.anode
  N6: Part1.D5_PWM, R1.Pin_0
  N7: Part1.D6_PWM, LED4.anode
  N8: Part1.5V, Q1.A, Q1.K, U1.E
  N9: Part1.GND, BAT1.-, Q1.C, Q2.2, U1.S, LED1.cathode, LED2.cathode, LED3.cathode, LED4.cathode, LED5.cathode
  N10: Part1.VIN, S2.COM
  N11: BAT1.+, BAT2.-
  N12: BAT2.+, BAT8.-
  N13: BAT3.-, BAT7.+
  N14: BAT3.+, S2.L2
  N15: BAT4.-, BAT8.+
  N16: BAT4.+, BAT7.-, M1.pin_2
  N17: Q2.0, R1.Pin_1
  N18: Q2.1, D1.cathode
  N19: D1.anode, M1.pin_1

notes:
  SCL
  SDA
